// Logisim project OZ-3.circ as structural Verilog: 22 circuits, main circuit Bench Test
module Bench_Test (
  input  [4:0] in_1
);

  wire clock_1_out, clock_2_out, clock_3_out, decoder_1_out1, decoder_1_out2, decoder_1_out3, decoder_1_out4,
       decoder_1_out5, decoder_1_out6, decoder_1_out7, decoder_1_out8, decoder_1_out9, decoder_1_out10,
       decoder_1_out11, decoder_1_out12, decoder_1_out13, decoder_1_out14, decoder_1_out15, decoder_2_out1,
       decoder_2_out2, decoder_2_out3, decoder_2_out4, decoder_2_out5, decoder_2_out6, decoder_2_out7,
       decoder_2_out8, decoder_2_out9, decoder_2_out10, decoder_2_out11, decoder_2_out12, decoder_2_out13,
       decoder_2_out14, decoder_2_out15, not_1_out, oz_3_1_dram_r_w, oz_3_1_op0;
  wire [3:0] joystick_1_x, joystick_1_y, joystick_2_x, joystick_2_y, oz_3_1_instruction,
       oz_3_1_instruction_2, oz_3_1_instruction_3, oz_3_1_instruction_4, oz_3_1_instruction_address;
  wire [15:0] decoder_3_out0, oz_3_1_instruction_5, register_1_q, register_2_q, register_3_q, register_4_q,
       register_5_q, register_6_q, register_7_q, register_8_q, register_9_q, register_10_q, register_11_q,
       register_12_q, register_13_q, register_14_q, register_15_q, register_16_q;
  wire [23:0] oz_3_1_dram_address, oz_3_1_instruction_address_2;
  wire [31:0] controlled_buffer_1_out, controlled_buffer_2_out, multiplexer_1_out, oz_3_1_dram_data_out,
       oz_3_1_oprt_out, oz_3_1_reg_data;

  Hex_Digit_Display hex_digit_display_1 (.value(oz_3_1_instruction_address_2[23:20]));  // open: dp
  Decoder #(.select(4), .tristate("false")) decoder_1 (
    .out1(decoder_1_out1), .out2(decoder_1_out2), .out3(decoder_1_out3), .out4(decoder_1_out4),
    .out5(decoder_1_out5), .out6(decoder_1_out6), .out7(decoder_1_out7), .out8(decoder_1_out8),
    .out9(decoder_1_out9), .out10(decoder_1_out10), .out11(decoder_1_out11), .out12(decoder_1_out12),
    .out13(decoder_1_out13), .out14(decoder_1_out14), .out15(decoder_1_out15), .sel(joystick_1_y));  // open: out0
  Joystick #(.bits(4)) joystick_1 (.x(joystick_1_x), .y(joystick_1_y));
  Hex_Digit_Display hex_digit_display_2 (.value(oz_3_1_instruction_address_2[19:16]));  // open: dp
  Hex_Digit_Display hex_digit_display_3 (.value(oz_3_1_instruction_address));  // open: dp
  Decoder #(.select(4), .tristate("false")) decoder_2 (
    .out1(decoder_2_out1), .out2(decoder_2_out2), .out3(decoder_2_out3), .out4(decoder_2_out4),
    .out5(decoder_2_out5), .out6(decoder_2_out6), .out7(decoder_2_out7), .out8(decoder_2_out8),
    .out9(decoder_2_out9), .out10(decoder_2_out10), .out11(decoder_2_out11), .out12(decoder_2_out12),
    .out13(decoder_2_out13), .out14(decoder_2_out14), .out15(decoder_2_out15), .sel(joystick_1_x));  // open: out0
  Hex_Digit_Display hex_digit_display_4 (.value(oz_3_1_instruction_address_2[7:4]));  // open: dp
  Hex_Digit_Display hex_digit_display_5 (.value(oz_3_1_instruction_address_2[11:8]));  // open: dp
  Hex_Digit_Display hex_digit_display_6 (.value(oz_3_1_instruction_address_2[3:0]));  // open: dp
  Hex_Digit_Display hex_digit_display_7 (.value(oz_3_1_instruction_4));  // open: dp
  Hex_Digit_Display hex_digit_display_8 (.value(oz_3_1_instruction_3));  // open: dp
  Joystick #(.bits(4)) joystick_2 (.x(joystick_2_x), .y(joystick_2_y));
  Hex_Digit_Display hex_digit_display_9 (.value(oz_3_1_instruction_2));  // open: dp
  Hex_Digit_Display hex_digit_display_10 (.value(oz_3_1_instruction));  // open: dp
  Decoder #(.select(4), .tristate("false")) decoder_3 (
    .out0(decoder_3_out0[0]), .out1(decoder_3_out0[1]), .out2(decoder_3_out0[2]), .out3(decoder_3_out0[3]),
    .out4(decoder_3_out0[4]), .out5(decoder_3_out0[5]), .out6(decoder_3_out0[6]), .out7(decoder_3_out0[7]),
    .out8(decoder_3_out0[8]), .out9(decoder_3_out0[9]), .out10(decoder_3_out0[10]),
    .out11(decoder_3_out0[11]), .out12(decoder_3_out0[12]), .out13(decoder_3_out0[13]),
    .out14(decoder_3_out0[14]), .out15(decoder_3_out0[15]), .sel(joystick_2_x));
  Hex_Digit_Display hex_digit_display_11 (.value(oz_3_1_instruction_5[11:8]));  // open: dp
  Hex_Digit_Display hex_digit_display_12 (.value(oz_3_1_instruction_5[15:12]));  // open: dp
  Hex_Digit_Display hex_digit_display_13 (.value(oz_3_1_instruction_5[7:4]));  // open: dp
  Hex_Digit_Display hex_digit_display_14 (.value(oz_3_1_instruction_5[3:0]));  // open: dp
  LED led_1 (.in(clock_1_out));
  Clock #(.highDuration(1), .lowDuration(1)) clock_1 (.out(clock_1_out));
  Multiplexer #(.select(1), .width(32)) multiplexer_1 (
    .in0({{16{1'b0}}, decoder_3_out0}), .in1({{28{1'b0}}, joystick_2_y}), .out(multiplexer_1_out),
    .sel(oz_3_1_op0));
  Hex_Digit_Display hex_digit_display_15 (.value({3'b000, in_1[4]}));  // open: dp
  OZ_3 oz_3_1 (
    .op0(oz_3_1_op0),
    .instruction_address({oz_3_1_instruction_address_2[23:16], oz_3_1_instruction_address, oz_3_1_instruction_address_2[11:0]}),
    .instruction({oz_3_1_instruction_4, oz_3_1_instruction_3, oz_3_1_instruction_2, oz_3_1_instruction, oz_3_1_instruction_5}),
    .reg_addr(in_1), .reg_data(oz_3_1_reg_data), .iprt_in(multiplexer_1_out), .oprt_out(oz_3_1_oprt_out),
    .dRAM_data_in(controlled_buffer_2_out), .dRAM_R_W(oz_3_1_dram_r_w), .dRAM_address(oz_3_1_dram_address),
    .dRAM_data_out(oz_3_1_dram_data_out));  // open: op1, op2, op3, op4, op5, op6, op7, op8, op9, op10, op11, op12, op13, op14, op15, ip0, ip1, ip2, ip3, ip4, ip5, ip6, ip7, ip8, ip9, ip10, ip11, ip12, ip13, ip14, ip15
  assign controlled_buffer_1_out = not_1_out ? oz_3_1_dram_data_out : 32'bz;  // Controlled_Buffer controlled_buffer_1
  not not_1 (not_1_out, oz_3_1_dram_r_w);
  assign controlled_buffer_2_out = oz_3_1_dram_r_w ? controlled_buffer_1_out : 32'bz;  // Controlled_Buffer controlled_buffer_2
  Hex_Digit_Display hex_digit_display_16 (.value(in_1[3:0]));  // open: dp
  Clock #(.highDuration(1), .lowDuration(1)) clock_2 (.out(clock_2_out));
  Hex_Digit_Display hex_digit_display_17 (.value(oz_3_1_reg_data[31:28]));  // open: dp
  RAM #(.addrWidth(24), .dataWidth(32), .bus("combined")) ram_1 (
    .addr(oz_3_1_dram_address), .data(controlled_buffer_1_out), .clk(clock_2_out), .ld(oz_3_1_dram_r_w));  // open: sel, clr
  Hex_Digit_Display hex_digit_display_18 (.value(oz_3_1_reg_data[23:20]));  // open: dp
  Hex_Digit_Display hex_digit_display_19 (.value(oz_3_1_reg_data[27:24]));  // open: dp
  Hex_Digit_Display hex_digit_display_20 (.value(oz_3_1_reg_data[15:12]));  // open: dp
  Hex_Digit_Display hex_digit_display_21 (.value(oz_3_1_reg_data[19:16]));  // open: dp
  Hex_Digit_Display hex_digit_display_22 (.value(oz_3_1_reg_data[7:4]));  // open: dp
  Hex_Digit_Display hex_digit_display_23 (.value(oz_3_1_reg_data[11:8]));  // open: dp
  Clock #(.highDuration(1), .lowDuration(1)) clock_3 (.out(clock_3_out));
  Hex_Digit_Display hex_digit_display_24 (.value(oz_3_1_reg_data[3:0]));  // open: dp
  Register #(.width(16), .trigger("rising")) register_1 (
    .D(oz_3_1_oprt_out[15:0]), .en(oz_3_1_oprt_out[31]), .Q(register_1_q), .clk(clock_3_out));  // open: clr
  Register #(.width(16), .trigger("rising")) register_2 (
    .D(oz_3_1_oprt_out[15:0]), .en(oz_3_1_oprt_out[30]), .Q(register_2_q), .clk(clock_3_out));  // open: clr
  Register #(.width(16), .trigger("rising")) register_3 (
    .D(oz_3_1_oprt_out[15:0]), .en(oz_3_1_oprt_out[29]), .Q(register_3_q), .clk(clock_3_out));  // open: clr
  Register #(.width(16), .trigger("rising")) register_4 (
    .D(oz_3_1_oprt_out[15:0]), .en(oz_3_1_oprt_out[28]), .Q(register_4_q), .clk(clock_3_out));  // open: clr
  Register #(.width(16), .trigger("rising")) register_5 (
    .D(oz_3_1_oprt_out[15:0]), .en(oz_3_1_oprt_out[27]), .Q(register_5_q), .clk(clock_3_out));  // open: clr
  Register #(.width(16), .trigger("rising")) register_6 (
    .D(oz_3_1_oprt_out[15:0]), .en(oz_3_1_oprt_out[26]), .Q(register_6_q), .clk(clock_3_out));  // open: clr
  Register #(.width(16), .trigger("rising")) register_7 (
    .D(oz_3_1_oprt_out[15:0]), .en(oz_3_1_oprt_out[25]), .Q(register_7_q), .clk(clock_3_out));  // open: clr
  Register #(.width(16), .trigger("rising")) register_8 (
    .D(oz_3_1_oprt_out[15:0]), .en(oz_3_1_oprt_out[24]), .Q(register_8_q), .clk(clock_3_out));  // open: clr
  Register #(.width(16), .trigger("rising")) register_9 (
    .D(oz_3_1_oprt_out[15:0]), .en(oz_3_1_oprt_out[23]), .Q(register_9_q), .clk(clock_3_out));  // open: clr
  Register #(.width(16), .trigger("rising")) register_10 (
    .D(oz_3_1_oprt_out[15:0]), .en(oz_3_1_oprt_out[22]), .Q(register_10_q), .clk(clock_3_out));  // open: clr
  Register #(.width(16), .trigger("rising")) register_11 (
    .D(oz_3_1_oprt_out[15:0]), .en(oz_3_1_oprt_out[21]), .Q(register_11_q), .clk(clock_3_out));  // open: clr
  Register #(.width(16), .trigger("rising")) register_12 (
    .D(oz_3_1_oprt_out[15:0]), .en(oz_3_1_oprt_out[20]), .Q(register_12_q), .clk(clock_3_out));  // open: clr
  Register #(.width(16), .trigger("rising")) register_13 (
    .D(oz_3_1_oprt_out[15:0]), .en(oz_3_1_oprt_out[19]), .Q(register_13_q), .clk(clock_3_out));  // open: clr
  Register #(.width(16), .trigger("rising")) register_14 (
    .D(oz_3_1_oprt_out[15:0]), .en(oz_3_1_oprt_out[18]), .Q(register_14_q), .clk(clock_3_out));  // open: clr
  Register #(.width(16), .trigger("rising")) register_15 (
    .D(oz_3_1_oprt_out[15:0]), .en(oz_3_1_oprt_out[17]), .Q(register_15_q), .clk(clock_3_out));  // open: clr
  Register #(.width(16), .trigger("rising")) register_16 (
    .D(oz_3_1_oprt_out[15:0]), .en(oz_3_1_oprt_out[16]), .Q(register_16_q), .clk(clock_3_out));  // open: clr
  DotMatrix #(.inputtype("row"), .matrixcols(16), .matrixrows(16), .dotshape("square")) dotmatrix_1 (
    .row0(register_1_q), .row1(register_2_q), .row2(register_3_q), .row3(register_4_q), .row4(register_5_q),
    .row5(register_6_q), .row6(register_7_q), .row7(register_8_q), .row8(register_9_q), .row9(register_10_q),
    .row10(register_11_q), .row11(register_12_q), .row12(register_13_q), .row13(register_14_q),
    .row14(register_15_q), .row15(register_16_q));

  // Notes on the sheet:
  //   instruction address
  //   instruction
  //   clock
  //   OZ-3
  //   reg addr
  //   dRAM
  //   reg data
endmodule

module OZ_3 (
  input  ip0,
  input  [4:0] reg_addr,
  input  ip1,
  input  ip2,
  input  ip3,
  input  ip4,
  input  ip5,
  input  ip6,
  input  ip7,
  input  ip8,
  input  ip9,
  input  ip10,
  input  ip11,
  input  ip12,
  input  ip13,
  input  ip14,
  input  [31:0] dRAM_data_in,
  input  ip15,
  input  [31:0] iprt_in,
  output [23:0] instruction_address,
  output [31:0] instruction,
  output [31:0] reg_data,
  output op0,
  output op1,
  output op2,
  output op3,
  output op4,
  output op5,
  output op6,
  output op7,
  output op8,
  output op9,
  output op10,
  output op11,
  output op12,
  output op13,
  output op14,
  output op15,
  output dRAM_R_W,
  output [23:0] dRAM_address,
  output [31:0] dRAM_data_out,
  output [31:0] oprt_out
);

  wire clock_1_out, clock_2_out, ex_1_cond_to_if, memio_1_data_to_opin_array, memio_1_to_cond_reg,
       memio_1_to_opin_array_clk, memio_1_to_oprt_reg_clk, wb_1_to_reg_file_we;
  wire [3:0] memio_1_to_opin_sel;
  wire [4:0] ex_1_result_reg_to_id, memio_1_result_reg_to_id, memio_1_to_reg_file_read,
       wb_1_result_reg_to_id, wb_1_to_reg_file_addr;
  wire [5:0] id_1_wb_cntl;
  wire [11:0] id_1_ex_cntl;
  wire [15:0] ipin_reg_q, or_1_out;
  wire [19:0] id_1_memio_cntl;
  wire [31:0] ex_1_alu_result_to_mem, id_1_alu__a, id_1_alu__b, id_1_r3_to_memio, if_1_instruction_to_id,
       if_1_to_iram_addr, iprt_reg_q, memio_1_to_dram_address, memio_1_to_oprt_reg_data,
       memio_1_to_wb_and_id, wb_1_forwarded_result_to_id, wb_1_to_reg_file_data;

  _32to24 u_32to24_1 (.\output (instruction_address), .\input (if_1_to_iram_addr));
  Opin_Array opin_array_1 (
    .p0(op0), .p1(op1), .p2(op2), .p3(op3), .p4(op4), .p5(op5), .p6(op6), .p7(op7), .p8(op8), .p9(op9),
    .p10(op10), .p11(op11), .p12(op12), .p13(op13), .p14(op14), .p15(op15),
    .data(memio_1_data_to_opin_array), .clock(memio_1_to_opin_array_clk), .sel(memio_1_to_opin_sel));
  Register #(.width(32), .trigger("rising")) iprt_reg (
    .D(iprt_in), .Q(iprt_reg_q), .clk(clock_1_out));  // open: en, clr
  Clock #(.highDuration(1), .lowDuration(1)) clock_1 (.out(clock_1_out));
  ROM #(.addrWidth(24), .dataWidth(32)) rom_1 (.addr(instruction_address), .data(instruction));  // open: sel
  IF if_1 (
    .from_cond_block(ex_1_cond_to_if), .ALU_result_from_MEM(ex_1_alu_result_to_mem),
    .to_iRAM_addr(if_1_to_iram_addr), .from_iRAM_data(instruction), .instruction_to_ID(if_1_instruction_to_id));
  Register #(.width(32), .trigger("rising")) oprt_reg (
    .D(memio_1_to_oprt_reg_data), .Q(oprt_out), .clk(memio_1_to_oprt_reg_clk));  // open: en, clr
  ID id_1 (
    .r3_addr_from_MEM(memio_1_to_reg_file_read), .w1_addr_from_WB(wb_1_to_reg_file_addr),
    .w1_data_from_WB(wb_1_to_reg_file_data), .w1_WE_from_WB(wb_1_to_reg_file_we),
    .Instruction_from_IF(if_1_instruction_to_id), .reg_addr(reg_addr), .reg_data_to_outer_edge(reg_data),
    .ALU__A(id_1_alu__a), .ALU__B(id_1_alu__b), .WB_cntl(id_1_wb_cntl), .MEMIO_cntl(id_1_memio_cntl),
    .r3_to_MEMIO(id_1_r3_to_memio), .EX_cntl(id_1_ex_cntl), .forward_from_EX(ex_1_alu_result_to_mem),
    .result_reg_from_EX(ex_1_result_reg_to_id), .forward_from_MEM(memio_1_to_wb_and_id),
    .result_reg_from_MEM(memio_1_result_reg_to_id), .forward_from_WB(wb_1_forwarded_result_to_id),
    .result_reg_from_WB(wb_1_result_reg_to_id));
  EX ex_1 (
    .p_flag_from_MEM(memio_1_to_cond_reg), .cond_to_IF(ex_1_cond_to_if), .ALU_A_from_ID(id_1_alu__a),
    .ALU_B_from_ID(id_1_alu__b), .ALU_result_to_MEM(ex_1_alu_result_to_mem), .from_ID(id_1_ex_cntl),
    .result_reg_to_ID(ex_1_result_reg_to_id));
  MEMIO memio_1 (
    .to_cond_reg(memio_1_to_cond_reg), .from_ipin_reg(ipin_reg_q),
    .to_opin_array_clk(memio_1_to_opin_array_clk), .to_opin_sel(memio_1_to_opin_sel),
    .data_to_opin_array(memio_1_data_to_opin_array), .from_iprt_reg_data(iprt_reg_q),
    .to_oprt_reg_data(memio_1_to_oprt_reg_data), .to_oprt_reg_clk(memio_1_to_oprt_reg_clk),
    .from_dRAM_data(dRAM_data_in), .to_dRAM_R_W(dRAM_R_W), .to_dRAM_address(memio_1_to_dram_address),
    .to_dRAM_data(dRAM_data_out), .to_reg_file_read(memio_1_to_reg_file_read),
    .ALU_Result(ex_1_alu_result_to_mem), .to_WB_and_ID(memio_1_to_wb_and_id), .from_ID(id_1_memio_cntl),
    .from_reg_file(id_1_r3_to_memio), .result_reg_to_ID(memio_1_result_reg_to_id));
  WB wb_1 (
    .to_Reg_File_data(wb_1_to_reg_file_data), .to_Reg_File_addr(wb_1_to_reg_file_addr),
    .to_Reg_File_WE(wb_1_to_reg_file_we), .from_MEMIO(memio_1_to_wb_and_id), .from_ID(id_1_wb_cntl),
    .result_reg_to_ID(wb_1_result_reg_to_id), .forwarded_result_to_ID(wb_1_forwarded_result_to_id));
  Clock #(.highDuration(1), .lowDuration(1)) clock_2 (.out(clock_2_out));
  Register #(.width(16), .trigger("rising")) ipin_reg (
    .D(or_1_out), .Q(ipin_reg_q), .clk(clock_2_out));  // open: en, clr
  _32to24 u_32to24_2 (.\output (dRAM_address), .\input (memio_1_to_dram_address));
  or or_1 (or_1_out[0], ip0, 1'b0);
  or or_2 (or_1_out[1], ip1, 1'b0);
  or or_3 (or_1_out[2], ip2, 1'b0);
  or or_4 (or_1_out[3], ip3, 1'b0);
  or or_5 (or_1_out[4], ip4, 1'b0);
  or or_6 (or_1_out[5], ip5, 1'b0);
  or or_7 (or_1_out[6], ip6, 1'b0);
  or or_8 (or_1_out[7], ip7, 1'b0);
  or or_9 (or_1_out[8], ip8, 1'b0);
  or or_10 (or_1_out[9], ip9, 1'b0);
  or or_11 (or_1_out[10], ip10, 1'b0);
  or or_12 (or_1_out[11], ip11, 1'b0);
  or or_13 (or_1_out[12], ip12, 1'b0);
  or or_14 (or_1_out[13], ip13, 1'b0);
  or or_15 (or_1_out[14], ip14, 1'b0);
  or or_16 (or_1_out[15], ip15, 1'b0);

  // Notes on the sheet:
  //   Ben Oztalay
  //   August, 2009
  //   trim
  //   opin
  //   iROM
  //   contents of rom_1 (hex, n*v repeats v):
  //   0 40820000 0 0 3c841802 44820000 54000000 0 50000000 48200000 0 48400000 0 0 40820000 0 0 3c840803
  //   44820000 4*0 40a00000 40c00001 40e00002 40800003 41200004 41400005 41600006 41000007 41a00008
  //   41c00009 41e0000a 4180000b 4220000c 42c0000d 42e0000e 4280000f 4c050000 4c060000 4c070000 4c080000
  //   4c090000 4c0a0000 4c0b0000 4c0c0000 4c0d0000 4c0e0000 4c0f0000 4c100000 4c110000 4c120000 4c130000
  //   4c140000 98000001
  //   IF
  //   ID
  //   EX
  //   MEM
  //   IO
  //   WB
  //   trim
endmodule

module IF (
  input  [31:0] from_iRAM_data,
  input  from_cond_block,
  input  [31:0] ALU_result_from_MEM,
  output [31:0] to_iRAM_addr,
  output [31:0] instruction_to_ID
);

  wire clock_1_out;
  wire [31:0] adder_1_out, multiplexer_1_out;

  Clock #(.highDuration(1), .lowDuration(1)) clock_1 (.out(clock_1_out));
  Multiplexer #(.select(1), .width(32)) multiplexer_1 (
    .in0(adder_1_out), .in1(ALU_result_from_MEM), .out(multiplexer_1_out), .sel(from_cond_block));
  Adder_part #(.width(32)) adder_1 (.a(to_iRAM_addr), .b(32'h1), .out(adder_1_out));  // open: cin, cout
  Register #(.width(32), .trigger("rising")) register_1 (
    .D(multiplexer_1_out), .Q(to_iRAM_addr), .clk(clock_1_out));  // open: en, clr
  // Probe on from_iRAM_data

  assign instruction_to_ID = from_iRAM_data;

  // Notes on the sheet:
  //   Ben Oztalay
  //   August, 2009
  //   PC
endmodule

module ID (
  input  [31:0] Instruction_from_IF,
  input  [4:0] reg_addr,
  input  [4:0] r3_addr_from_MEM,
  input  [4:0] w1_addr_from_WB,
  input  [31:0] w1_data_from_WB,
  input  w1_WE_from_WB,
  input  [31:0] forward_from_EX,
  input  [4:0] result_reg_from_EX,
  input  [31:0] forward_from_MEM,
  input  [4:0] result_reg_from_MEM,
  input  [31:0] forward_from_WB,
  input  [4:0] result_reg_from_WB,
  output [31:0] reg_data_to_outer_edge,
  output [5:0] WB_cntl,
  output [19:0] MEMIO_cntl,
  output [31:0] r3_to_MEMIO,
  output [11:0] EX_cntl,
  output [31:0] ALU__A,
  output [31:0] ALU__B
);

  wire and_2_out, and_5_out, and_6_out, and_7_out, and_8_out, and_9_out, and_10_out, clock_1_out,
       decoder_1_out0, decoder_1_out4, decoder_1_out5, n5bitcomp_1_out_3, n5bitcomp_2_out_3,
       n5bitcomp_3_out_3, n5bitcomp_4_out_3, n5bitcomp_5_out_3, n5bitcomp_6_out_3, n5bitcomp_7_out_3,
       n5bitcomp_8_out_3, n5bitcomp_9_out_3, not_1_out, not_2_out, not_3_out, not_4_out, not_5_out,
       not_6_out, not_7_out, not_8_out, not_9_out, not_10_out, not_11_out, not_12_out, or_3_out,
       priority_encoder_1_p1, priority_encoder_1_p3, priority_encoder_1_p4, priority_encoder_1_p5,
       priority_encoder_1_p6, priority_encoder_1_p7, priority_encoder_2_p2, priority_encoder_2_p4,
       priority_encoder_2_p6;
  wire [2:0] or_7_out_3, or_9_out_3;
  wire [4:0] controlled_buffer_10_out, demultiplexer_1_out0, or_7_out_2, or_9_out, or_9_out_2, or_10_out,
       or_16_out, or_17_out;
  wire [15:0] or_9_out_5;
  wire [20:0] or_7_out;
  wire [31:0] controlled_buffer_1_out, controlled_buffer_2_out, controlled_buffer_3_out,
       controlled_buffer_4_out, controlled_buffer_5_out, controlled_buffer_6_out, controlled_buffer_7_out,
       controlled_buffer_8_out, controlled_buffer_9_out, controlled_buffer_11_out, controlled_buffer_12_out,
       controlled_buffer_13_out, controlled_buffer_14_out, instruction_q, n16to32signex_1_output,
       n16to32signex_2_output, n21to32signex_1_output, or_12_out, or_14_out, or_15_out, or_19_out, or_20_out,
       or_21_out, register_file_1_read_out_1, register_file_1_read_out_2;
  wire [31:29] or_7_out_4, or_9_out_4;

  assign EX_cntl[6:4] = 3'b000 | or_7_out_3;  // OR_Gate or_1, 3 bits wide
  _21to32signex u_21to32signex_1 (.\input (or_7_out), .\output (n21to32signex_1_output));
  or or_2 (MEMIO_cntl[6], 1'b0, priority_encoder_1_p4);
  or or_3 (or_3_out, priority_encoder_1_p4, MEMIO_cntl[11]);
  // Priority_Encoder #(.select(1)) priority_encoder_1: pin names not known; wires that end beside it: priority_encoder_1_p1, priority_encoder_1_p1, priority_encoder_1_p3, priority_encoder_1_p4, priority_encoder_1_p5, priority_encoder_1_p6, priority_encoder_1_p7
  or or_4 (MEMIO_cntl[5], 1'b0, MEMIO_cntl[11]);
  and and_1 (MEMIO_cntl[14], priority_encoder_1_p5, priority_encoder_1_p7);
  not not_1 (not_1_out, or_9_out_4[31]);
  and and_2 (and_2_out, not_1_out, or_9_out_4[30], not_2_out);
  not not_2 (not_2_out, or_9_out_4[29]);
  Decoder #(.select(3), .tristate("false")) decoder_1 (
    .out0(decoder_1_out0), .out1(priority_encoder_1_p6), .out2(MEMIO_cntl[11]), .out3(MEMIO_cntl[12]),
    .out4(decoder_1_out4), .out5(decoder_1_out5), .out6(MEMIO_cntl[9]), .sel(or_9_out_3));  // open: out7
  and and_3 (priority_encoder_1_p4, and_2_out, decoder_1_out0);
  or or_5 (MEMIO_cntl[13], priority_encoder_1_p4, priority_encoder_1_p6);
  or or_6 (MEMIO_cntl[10], MEMIO_cntl[11], MEMIO_cntl[12]);
  assign controlled_buffer_1_out = instruction_q[31] ? instruction_q : 32'bz;  // Controlled_Buffer controlled_buffer_1
  assign {or_7_out_4, or_7_out_3, or_7_out_2, or_7_out} = controlled_buffer_1_out | {32{1'b0}};  // OR_Gate or_7, 32 bits wide
  or or_8 (MEMIO_cntl[7], decoder_1_out4, decoder_1_out5);
  // Priority_Encoder #(.select(1)) priority_encoder_2: pin names not known; wires that end beside it: decoder_1_out5, priority_encoder_2_p2, decoder_1_out4, priority_encoder_2_p4, priority_encoder_1_p3, priority_encoder_2_p6, priority_encoder_2_p6
  and and_4 (MEMIO_cntl[8], priority_encoder_2_p2, priority_encoder_2_p4);
  Clock #(.highDuration(1), .lowDuration(1)) clock_1 (.out(clock_1_out));
  assign controlled_buffer_2_out = instruction_q[30] ? instruction_q : 32'bz;  // Controlled_Buffer controlled_buffer_2
  assign {or_9_out_4, or_9_out_3, or_9_out_2, or_9_out, or_9_out_5} = controlled_buffer_2_out | {32{1'b0}};  // OR_Gate or_9, 32 bits wide
  Demultiplexer #(.select(1), .width(5), .tristate("false")) demultiplexer_1 (
    .out0(demultiplexer_1_out0), .out1(MEMIO_cntl[4:0]), .in(or_9_out_2), .sel(priority_encoder_1_p6));
  assign or_10_out = or_7_out_2 | or_9_out | or_12_out[20:16];  // OR_Gate or_10, 5 bits wide
  Register_File register_file_1 (
    .write_enable(w1_WE_from_WB), .write_adress(w1_addr_from_WB), .write_data(w1_data_from_WB),
    .read_adr_4(reg_addr), .read_adr_3(r3_addr_from_MEM), .read_adr_2(or_17_out), .read_adr_1(or_10_out),
    .read_out_4(reg_data_to_outer_edge), .read_out_1(register_file_1_read_out_1),
    .read_out_2(register_file_1_read_out_2), .read_out_3(r3_to_MEMIO));
  assign ALU__A = register_file_1_read_out_1 | or_14_out;  // OR_Gate or_11, 32 bits wide
  Register #(.width(32), .trigger("rising")) instruction (
    .D(Instruction_from_IF), .Q(instruction_q), .clk(clock_1_out));  // open: en, clr
  _16to32signex u_16to32signex_1 (.\input (or_9_out_5), .\output (n16to32signex_1_output));
  assign controlled_buffer_3_out = instruction_q[29] ? instruction_q : 32'bz;  // Controlled_Buffer controlled_buffer_3
  assign or_12_out = controlled_buffer_3_out | {32{1'b0}};  // OR_Gate or_12, 32 bits wide
  assign ALU__B = register_file_1_read_out_2 | n21to32signex_1_output | n16to32signex_1_output | controlled_buffer_11_out | or_15_out;  // OR_Gate or_13, 32 bits wide
  not not_3 (not_3_out, or_12_out[30]);
  not not_4 (not_4_out, or_12_out[31]);
  and and_5 (and_5_out, not_4_out, not_3_out, or_12_out[29]);
  and and_6 (and_6_out, or_12_out[28], or_12_out[27], or_12_out[26]);
  Multiplexer #(.select(1), .width(4)) multiplexer_1 (
    .in0({1'b0, or_12_out[28:26]}), .in1(or_12_out[3:0]), .out(EX_cntl[3:0]), .sel(and_6_out));
  assign or_14_out = controlled_buffer_5_out | controlled_buffer_6_out | controlled_buffer_4_out;  // OR_Gate or_14, 32 bits wide
  assign controlled_buffer_4_out = and_7_out ? or_21_out : 32'bz;  // Controlled_Buffer controlled_buffer_4
  and and_7 (and_7_out, not_6_out, not_7_out, n5bitcomp_3_out_3);
  assign or_15_out = controlled_buffer_7_out | controlled_buffer_8_out | controlled_buffer_9_out;  // OR_Gate or_15, 32 bits wide
  not not_5 (not_5_out, n5bitcomp_5_out_3);
  assign or_16_out = or_9_out | or_12_out[20:16];  // OR_Gate or_16, 5 bits wide
  assign controlled_buffer_5_out = n5bitcomp_1_out_3 ? or_19_out : 32'bz;  // Controlled_Buffer controlled_buffer_5
  not not_6 (not_6_out, n5bitcomp_1_out_3);
  assign controlled_buffer_6_out = and_8_out ? or_20_out : 32'bz;  // Controlled_Buffer controlled_buffer_6
  and and_8 (and_8_out, not_6_out, n5bitcomp_2_out_3);
  not not_7 (not_7_out, n5bitcomp_2_out_3);
  assign controlled_buffer_7_out = n5bitcomp_4_out_3 ? or_19_out : 32'bz;  // Controlled_Buffer controlled_buffer_7
  not not_8 (not_8_out, n5bitcomp_4_out_3);
  assign controlled_buffer_8_out = and_9_out ? or_20_out : 32'bz;  // Controlled_Buffer controlled_buffer_8
  and and_9 (and_9_out, not_8_out, n5bitcomp_5_out_3);
  and and_10 (and_10_out, n5bitcomp_6_out_3, not_5_out, not_8_out);
  assign controlled_buffer_9_out = and_10_out ? or_21_out : 32'bz;  // Controlled_Buffer controlled_buffer_9
  assign controlled_buffer_10_out = and_6_out ? or_12_out[15:11] : 5'bz;  // Controlled_Buffer controlled_buffer_10
  assign or_17_out = {5{1'b0}} | controlled_buffer_10_out;  // OR_Gate or_17, 5 bits wide
  _5bitComp u_5bitcomp_1 (.out_3(n5bitcomp_1_out_3), .A(or_16_out), .B(result_reg_from_EX));
  _5bitComp u_5bitcomp_2 (.out_3(n5bitcomp_2_out_3), .A(or_16_out), .B(result_reg_from_MEM));
  _5bitComp u_5bitcomp_3 (.out_3(n5bitcomp_3_out_3), .A(or_16_out), .B(result_reg_from_WB));
  _5bitComp u_5bitcomp_4 (.out_3(n5bitcomp_4_out_3), .A(or_17_out), .B(result_reg_from_EX));
  _5bitComp u_5bitcomp_5 (.out_3(n5bitcomp_5_out_3), .A(or_17_out), .B(result_reg_from_MEM));
  _5bitComp u_5bitcomp_6 (.out_3(n5bitcomp_6_out_3), .A(or_17_out), .B(result_reg_from_WB));
  _16to32signex u_16to32signex_2 (.\input (or_12_out[15:0]), .\output (n16to32signex_2_output));
  not not_9 (not_9_out, and_6_out);
  assign controlled_buffer_11_out = not_9_out ? n16to32signex_2_output : 32'bz;  // Controlled_Buffer controlled_buffer_11
  assign EX_cntl[11:7] = demultiplexer_1_out0 | or_12_out[25:21];  // OR_Gate or_18, 5 bits wide
  assign or_19_out = {32{1'b0}} | controlled_buffer_12_out;  // OR_Gate or_19, 32 bits wide
  assign controlled_buffer_12_out = not_10_out ? forward_from_EX : 32'bz;  // Controlled_Buffer controlled_buffer_12
  not not_10 (not_10_out, n5bitcomp_7_out_3);
  _5bitComp u_5bitcomp_7 (.out_3(n5bitcomp_7_out_3), .A({5{1'b0}}), .B(result_reg_from_EX));
  assign or_20_out = {32{1'b0}} | controlled_buffer_13_out;  // OR_Gate or_20, 32 bits wide
  assign controlled_buffer_13_out = not_11_out ? forward_from_MEM : 32'bz;  // Controlled_Buffer controlled_buffer_13
  not not_11 (not_11_out, n5bitcomp_8_out_3);
  _5bitComp u_5bitcomp_8 (.out_3(n5bitcomp_8_out_3), .A({5{1'b0}}), .B(result_reg_from_MEM));
  assign or_21_out = {32{1'b0}} | controlled_buffer_14_out;  // OR_Gate or_21, 32 bits wide
  assign controlled_buffer_14_out = not_12_out ? forward_from_WB : 32'bz;  // Controlled_Buffer controlled_buffer_14
  not not_12 (not_12_out, n5bitcomp_9_out_3);
  _5bitComp u_5bitcomp_9 (.out_3(n5bitcomp_9_out_3), .A({5{1'b0}}), .B(result_reg_from_WB));
  or or_22 (WB_cntl[0], or_3_out, and_5_out);

  assign MEMIO_cntl[19:15] = EX_cntl[11:7];
  assign WB_cntl[5:1] = EX_cntl[11:7];

  // Notes on the sheet:
  //   Ben Oztalay
  //   August, 2009
  //   to EX for cond block
  //   src1
  //   Control Instructions
  //   signex
  //   disp to ALU B
  //   MUX cntl
  //   MEM
  //   iRAM cntl
  //   L/S
  //   reg file
  //   WE to WB
  //   Port cntl
  //   MEM
  //   a
  //   s
  //   a
  //   l
  //   to WB
  //   Pin ctl
  //   MEM
  //   01a
  //   01d
  //   Register File
  //   src1
  //   dest
  //   str data
  //   to MEM
  //   pchk
  //   MEMIO Instructions
  //   imm to ALU B
  //   reg file
  //   ALU cntl out
  //   WE to WB
  //   dest reg
  //   to WB
  //   Discombobulated forwarding logic
  //   ALU Instructions
  //   src1 reg
  //   src2 rg
  //   comp
  //   comp
  //   comp
  //   comp
  //   comp
  //   comp
  //   signex
  //   imm to ALU B
endmodule

module EX (
  input  [31:0] ALU_A_from_ID,
  input  [31:0] ALU_B_from_ID,
  input  p_flag_from_MEM,
  input  [11:0] from_ID,
  output cond_to_IF,
  output [31:0] ALU_result_to_MEM,
  output [4:0] result_reg_to_ID
);

  wire clock_1_out, clock_2_out, clock_3_out, clock_4_out;
  wire [2:0] register_5_q;
  wire [3:0] alu_1_condition_bits, register_2_q, register_4_q;
  wire [31:0] register_1_q, register_3_q;

  Condition_Block condition_block_1 (
    .output_to_IF(cond_to_IF), .flags({p_flag_from_MEM, register_2_q}), .cntl_from_ID(register_5_q));
  Register #(.width(32), .trigger("rising")) register_1 (
    .D(ALU_A_from_ID), .Q(register_1_q), .clk(clock_1_out));  // open: en, clr
  Clock #(.highDuration(1), .lowDuration(1)) clock_1 (.out(clock_1_out));
  Register #(.width(4), .trigger("rising")) register_2 (
    .D(alu_1_condition_bits), .Q(register_2_q), .clk(clock_2_out));  // open: en, clr
  Clock #(.highDuration(1), .lowDuration(1)) clock_2 (.out(clock_2_out));
  ALU alu_1 (
    .A(register_1_q), .B(register_3_q), .Condition_Bits(alu_1_condition_bits), .Result(ALU_result_to_MEM),
    .Cntl(register_4_q));
  Register #(.width(32), .trigger("rising")) register_3 (
    .D(ALU_B_from_ID), .Q(register_3_q), .clk(clock_3_out));  // open: en, clr
  Register #(.width(4), .trigger("rising")) register_4 (
    .D(from_ID[3:0]), .Q(register_4_q), .clk(clock_3_out));  // open: en, clr
  Register #(.width(8), .trigger("rising")) register_5 (
    .D(from_ID[11:4]), .Q({result_reg_to_ID, register_5_q}), .clk(clock_4_out));  // open: en, clr
  Clock #(.highDuration(1), .lowDuration(1)) clock_3 (.out(clock_3_out));
  Clock #(.highDuration(1), .lowDuration(1)) clock_4 (.out(clock_4_out));

  // Notes on the sheet:
  //   Ben Oztalay
  //   August, 2009
  //   Condition Block
  //   ALU input regs
  //   1-stage buf
  //   and IF and ID
  //   ALU
  //   1-stage buf
  //   1-stage buffer
endmodule

module MEMIO (
  input  [19:0] from_ID,
  input  [31:0] ALU_Result,
  input  [15:0] from_ipin_reg,
  input  [31:0] from_reg_file,
  input  [31:0] from_iprt_reg_data,
  input  [31:0] from_dRAM_data,
  output to_cond_reg,
  output [4:0] result_reg_to_ID,
  output to_opin_array_clk,
  output [3:0] to_opin_sel,
  output data_to_opin_array,
  output [31:0] to_oprt_reg_data,
  output to_oprt_reg_clk,
  output to_dRAM_R_W,
  output [31:0] to_dRAM_address,
  output [31:0] to_dRAM_data,
  output [31:0] to_WB_and_ID,
  output [4:0] to_reg_file_read
);

  wire and_5_out, and_6_out, and_7_out, clock_1_out, clock_2_out, clock_3_out, multiplexer_1_out, not_1_out;
  wire [1:0] register_2_q_2, register_2_q_3;
  wire [2:0] register_2_q;
  wire [2:1] register_2_q_4;
  wire [19:0] register_3_q;
  wire [31:0] controlled_buffer_1_out, controlled_buffer_3_out, register_1_q;

  Clock #(.highDuration(1), .lowDuration(1)) clock_1 (.out(clock_1_out));
  and and_1 (to_oprt_reg_clk, clock_1_out, and_6_out);
  Multiplexer #(.select(4), .width(1)) multiplexer_1 (
    .in0(from_ipin_reg[0]), .in1(from_ipin_reg[1]), .in2(from_ipin_reg[2]), .in3(from_ipin_reg[3]),
    .in4(from_ipin_reg[4]), .in5(from_ipin_reg[5]), .in6(from_ipin_reg[6]), .in7(from_ipin_reg[7]),
    .in8(from_ipin_reg[8]), .in9(from_ipin_reg[9]), .in10(from_ipin_reg[10]), .in11(from_ipin_reg[11]),
    .in12(from_ipin_reg[12]), .in13(from_ipin_reg[13]), .in14(from_ipin_reg[14]), .in15(from_ipin_reg[15]),
    .out(multiplexer_1_out), .sel(to_opin_sel));
  assign controlled_buffer_1_out = and_5_out ? from_iprt_reg_data : 32'bz;  // Controlled_Buffer controlled_buffer_1
  assign to_oprt_reg_data = and_6_out ? register_1_q : 32'bz;  // Controlled_Buffer controlled_buffer_2
  assign controlled_buffer_3_out = to_dRAM_R_W ? from_dRAM_data : 32'bz;  // Controlled_Buffer controlled_buffer_3
  assign to_dRAM_data = and_7_out ? from_reg_file : 32'bz;  // Controlled_Buffer controlled_buffer_4
  and and_2 (to_cond_reg, multiplexer_1_out, register_2_q_4[2]);
  and and_3 (data_to_opin_array, to_opin_array_clk, register_2_q_4[1]);
  _32to4 u_32to4_1 (.\output (to_opin_sel), .\input (register_1_q));
  and and_4 (to_dRAM_R_W, 1'b1, not_1_out);
  not not_1 (not_1_out, and_7_out);
  and and_5 (and_5_out, register_2_q[0], register_2_q[1]);
  and and_6 (and_6_out, register_2_q[2], register_2_q[0]);
  and and_7 (and_7_out, register_2_q_3[0], register_2_q_3[1]);
  assign to_dRAM_address = register_2_q_3[0] ? register_1_q : 32'bz;  // Controlled_Buffer controlled_buffer_5
  Register #(.width(32), .trigger("rising")) register_1 (
    .D(ALU_Result), .Q(register_1_q), .clk(clock_2_out));  // open: en, clr
  Clock #(.highDuration(1), .lowDuration(1)) clock_2 (.out(clock_2_out));
  Multiplexer #(.select(2), .width(32)) multiplexer_2 (
    .in0(register_1_q), .in1(controlled_buffer_1_out), .in2(controlled_buffer_3_out), .in3({32{1'b0}}),
    .out(to_WB_and_ID), .sel(register_2_q_2));
  Register #(.width(20), .trigger("rising")) register_2 (
    .D(register_3_q),
    .Q({result_reg_to_ID, register_2_q_3, register_2_q, register_2_q_4, to_opin_array_clk, register_2_q_2, to_reg_file_read}),
    .clk(clock_3_out));  // open: en, clr
  Register #(.width(20), .trigger("rising")) register_3 (
    .D(from_ID), .Q(register_3_q), .clk(clock_3_out));  // open: en, clr
  Clock #(.highDuration(1), .lowDuration(1)) clock_3 (.out(clock_3_out));

  // Notes on the sheet:
  //   Ben Oztalay
  //   August, 2009
  //   Pin control
  //   Port control
  //   RAM control
  //   trimmer
  //   s
  //   ap01
  //   p01
  //   pc
  //   l
  //   a
  //   a
  //   s?
  //   2-stage buffer
  //   Control lines
endmodule

module WB (
  input  [5:0] from_ID,
  input  [31:0] from_MEMIO,
  output [4:0] result_reg_to_ID,
  output [31:0] to_Reg_File_data,
  output [31:0] forwarded_result_to_ID,
  output [4:0] to_Reg_File_addr,
  output to_Reg_File_WE
);

  wire clock_1_out, clock_2_out;
  wire [5:0] register_2_q, register_4_q;

  Register #(.width(32), .trigger("rising")) register_1 (
    .D(from_MEMIO), .Q(forwarded_result_to_ID), .clk(clock_1_out));  // open: en, clr
  Clock #(.highDuration(1), .lowDuration(1)) clock_1 (.out(clock_1_out));
  Register #(.width(6), .trigger("rising")) register_2 (
    .D(from_ID), .Q(register_2_q), .clk(clock_2_out));  // open: en, clr
  Register #(.width(6), .trigger("rising")) register_3 (
    .D(register_4_q), .Q({result_reg_to_ID, to_Reg_File_WE}), .clk(clock_2_out));  // open: en, clr
  Register #(.width(6), .trigger("rising")) register_4 (
    .D(register_2_q), .Q(register_4_q), .clk(clock_2_out));  // open: en, clr
  Clock #(.highDuration(1), .lowDuration(1)) clock_2 (.out(clock_2_out));

  assign to_Reg_File_addr = result_reg_to_ID;
  assign to_Reg_File_data = forwarded_result_to_ID;

  // Notes on the sheet:
  //   Ben Oztalay
  //   August, 2009
  //   Result reg
  //   3-stage buffer
endmodule

module ALU (
  input  [31:0] A,
  input  [31:0] B,
  input  [3:0] Cntl,
  output [31:0] Result,
  output [3:0] Condition_Bits
);

  wire alublock0_1_cout, alublock_1_cout, alublock_2_cout, alublock_3_cout, alublock_4_cout, alublock_5_cout,
       alublock_6_cout, alublock_7_cout, alublock_8_cout, alublock_9_cout, alublock_10_cout,
       alublock_11_cout, alublock_12_cout, alublock_13_cout, alublock_14_cout, alublock_15_cout,
       alublock_16_cout, alublock_17_cout, alublock_18_cout, alublock_19_cout, alublock_20_cout,
       alublock_21_cout, alublock_22_cout, alublock_23_cout, alublock_24_cout, alublock_25_cout,
       alublock_26_cout, alublock_27_cout, alublock_28_cout, alublock_29_cout, alublock_30_cout;

  ALUblock alublock_1 (
    .Cout(alublock_1_cout), .Cntl(Cntl), .Ai_1(A[31]), .A(A[30]), .Ai_1_2(A[29]), .B(B[30]), .S(Result[30]),
    .Cin(alublock_2_cout));
  ALUblock31 alublock31_1 (
    .Cout(Condition_Bits[0]), .Cntl(Cntl), .Ai_1(A[0]), .A(A[31]), .Ai_1_2(A[30]), .B(B[31]), .S(Result[31]),
    .Cin(alublock_1_cout));
  ALUblock alublock_2 (
    .Cout(alublock_2_cout), .Cntl(Cntl), .Ai_1(A[30]), .A(A[29]), .Ai_1_2(A[28]), .B(B[29]), .S(Result[29]),
    .Cin(alublock_3_cout));
  ALUblock alublock_3 (
    .Cout(alublock_3_cout), .Cntl(Cntl), .Ai_1(A[29]), .A(A[28]), .Ai_1_2(A[27]), .B(B[28]), .S(Result[28]),
    .Cin(alublock_4_cout));
  ALUblock alublock_4 (
    .Cout(alublock_4_cout), .Cntl(Cntl), .Ai_1(A[28]), .A(A[27]), .Ai_1_2(A[26]), .B(B[27]), .S(Result[27]),
    .Cin(alublock_5_cout));
  ALUblock alublock_5 (
    .Cout(alublock_5_cout), .Cntl(Cntl), .Ai_1(A[27]), .A(A[26]), .Ai_1_2(A[25]), .B(B[26]), .S(Result[26]),
    .Cin(alublock_6_cout));
  ALUblock alublock_6 (
    .Cout(alublock_6_cout), .Cntl(Cntl), .Ai_1(A[26]), .A(A[25]), .Ai_1_2(A[24]), .B(B[25]), .S(Result[25]),
    .Cin(alublock_7_cout));
  ALUblock alublock_7 (
    .Cout(alublock_7_cout), .Cntl(Cntl), .Ai_1(A[25]), .A(A[24]), .Ai_1_2(A[23]), .B(B[24]), .S(Result[24]),
    .Cin(alublock_8_cout));
  ALUblock alublock_8 (
    .Cout(alublock_8_cout), .Cntl(Cntl), .Ai_1(A[24]), .A(A[23]), .Ai_1_2(A[22]), .B(B[23]), .S(Result[23]),
    .Cin(alublock_9_cout));
  ALUblock alublock_9 (
    .Cout(alublock_9_cout), .Cntl(Cntl), .Ai_1(A[23]), .A(A[22]), .Ai_1_2(A[21]), .B(B[22]), .S(Result[22]),
    .Cin(alublock_10_cout));
  ALUblock alublock_10 (
    .Cout(alublock_10_cout), .Cntl(Cntl), .Ai_1(A[22]), .A(A[21]), .Ai_1_2(A[20]), .B(B[21]), .S(Result[21]),
    .Cin(alublock_11_cout));
  ALUblock alublock_11 (
    .Cout(alublock_11_cout), .Cntl(Cntl), .Ai_1(A[21]), .A(A[20]), .Ai_1_2(A[19]), .B(B[20]), .S(Result[20]),
    .Cin(alublock_12_cout));
  ALUblock alublock_12 (
    .Cout(alublock_12_cout), .Cntl(Cntl), .Ai_1(A[20]), .A(A[19]), .Ai_1_2(A[18]), .B(B[19]), .S(Result[19]),
    .Cin(alublock_13_cout));
  ALUblock alublock_13 (
    .Cout(alublock_13_cout), .Cntl(Cntl), .Ai_1(A[19]), .A(A[18]), .Ai_1_2(A[17]), .B(B[18]), .S(Result[18]),
    .Cin(alublock_14_cout));
  ALUblock alublock_14 (
    .Cout(alublock_14_cout), .Cntl(Cntl), .Ai_1(A[18]), .A(A[17]), .Ai_1_2(A[16]), .B(B[17]), .S(Result[17]),
    .Cin(alublock_15_cout));
  ALUblock alublock_15 (
    .Cout(alublock_15_cout), .Cntl(Cntl), .Ai_1(A[17]), .A(A[16]), .Ai_1_2(A[15]), .B(B[16]), .S(Result[16]),
    .Cin(alublock_16_cout));
  ALUblock alublock_16 (
    .Cout(alublock_16_cout), .Cntl(Cntl), .Ai_1(A[16]), .A(A[15]), .Ai_1_2(A[14]), .B(B[15]), .S(Result[15]),
    .Cin(alublock_17_cout));
  ALUblock alublock_17 (
    .Cout(alublock_17_cout), .Cntl(Cntl), .Ai_1(A[15]), .A(A[14]), .Ai_1_2(A[13]), .B(B[14]), .S(Result[14]),
    .Cin(alublock_18_cout));
  ALUblock alublock_18 (
    .Cout(alublock_18_cout), .Cntl(Cntl), .Ai_1(A[14]), .A(A[13]), .Ai_1_2(A[12]), .B(B[13]), .S(Result[13]),
    .Cin(alublock_19_cout));
  ALUblock alublock_19 (
    .Cout(alublock_19_cout), .Cntl(Cntl), .Ai_1(A[13]), .A(A[12]), .Ai_1_2(A[11]), .B(B[12]), .S(Result[12]),
    .Cin(alublock_20_cout));
  ALUblock alublock_20 (
    .Cout(alublock_20_cout), .Cntl(Cntl), .Ai_1(A[12]), .A(A[11]), .Ai_1_2(A[10]), .B(B[11]), .S(Result[11]),
    .Cin(alublock_21_cout));
  ALUblock alublock_21 (
    .Cout(alublock_21_cout), .Cntl(Cntl), .Ai_1(A[11]), .A(A[10]), .Ai_1_2(A[9]), .B(B[10]), .S(Result[10]),
    .Cin(alublock_22_cout));
  ALUblock alublock_22 (
    .Cout(alublock_22_cout), .Cntl(Cntl), .Ai_1(A[10]), .A(A[9]), .Ai_1_2(A[8]), .B(B[9]), .S(Result[9]),
    .Cin(alublock_23_cout));
  ALUblock alublock_23 (
    .Cout(alublock_23_cout), .Cntl(Cntl), .Ai_1(A[9]), .A(A[8]), .Ai_1_2(A[7]), .B(B[8]), .S(Result[8]),
    .Cin(alublock_25_cout));
  ALUblock alublock_24 (
    .Cout(alublock_24_cout), .Cntl(Cntl), .Ai_1(A[7]), .A(A[6]), .Ai_1_2(A[5]), .B(B[6]), .S(Result[6]),
    .Cin(alublock_26_cout));
  ALUblock alublock_25 (
    .Cout(alublock_25_cout), .Cntl(Cntl), .Ai_1(A[8]), .A(A[7]), .Ai_1_2(A[6]), .B(B[7]), .S(Result[7]),
    .Cin(alublock_24_cout));
  ALUblock alublock_26 (
    .Cout(alublock_26_cout), .Cntl(Cntl), .Ai_1(A[6]), .A(A[5]), .Ai_1_2(A[4]), .B(B[5]), .S(Result[5]),
    .Cin(alublock_27_cout));
  Comparator #(.width(32), .mode("twosComplement")) comparator_1 (
    .a(A), .b(B), .gt(Condition_Bits[1]), .eq(Condition_Bits[2]), .lt(Condition_Bits[3]));
  ALUblock alublock_27 (
    .Cout(alublock_27_cout), .Cntl(Cntl), .Ai_1(A[5]), .A(A[4]), .Ai_1_2(A[3]), .B(B[4]), .S(Result[4]),
    .Cin(alublock_28_cout));
  ALUblock alublock_28 (
    .Cout(alublock_28_cout), .Cntl(Cntl), .Ai_1(A[4]), .A(A[3]), .Ai_1_2(A[2]), .B(B[3]), .S(Result[3]),
    .Cin(alublock_29_cout));
  ALUblock alublock_29 (
    .Cout(alublock_29_cout), .Cntl(Cntl), .Ai_1(A[3]), .A(A[2]), .Ai_1_2(A[1]), .B(B[2]), .S(Result[2]),
    .Cin(alublock_30_cout));
  ALUblock0 alublock0_1 (
    .Cout(alublock0_1_cout), .Cntl(Cntl), .Ai_1(A[2]), .A(A[0]), .Ai_1_2(A[31]), .B(B[0]), .S(Result[0]));
  ALUblock alublock_30 (
    .Cout(alublock_30_cout), .Cntl(Cntl), .Ai_1(A[2]), .A(A[1]), .Ai_1_2(A[0]), .B(B[1]), .S(Result[1]),
    .Cin(alublock0_1_cout));

  // Notes on the sheet:
  //   Ben Oztalay
  //   August, 2009
  //   ALU31
  //   ALU30
  //   ALU29
  //   ALU28
  //   ALU27
  //   ALU26
  //   ALU25
  //   ALU24
  //   ALU23
  //   ALU22
  //   ALU21
  //   ALU20
  //   ALU19
  //   ALU18
  //   ALU17
  //   ALU16
  //   ALU15
  //   ALU14
  //   ALU13
  //   ALU12
  //   ALU11
  //   ALU9
  //   ALU10
  //   ALU8
  //   ALU7
  //   ALU6
  //   ALU5
  //   ALU4
  //   ALU3
  //   ALU2
  //   ALU1
  //   ALU0
endmodule

module Opin_Array (
  input  data,
  input  clock,
  input  [3:0] sel,
  output p0,
  output p1,
  output p2,
  output p3,
  output p4,
  output p5,
  output p6,
  output p7,
  output p8,
  output p9,
  output p10,
  output p11,
  output p12,
  output p13,
  output p14,
  output p15
);

  wire decoder_1_out0, decoder_1_out1, decoder_1_out2, decoder_1_out3, decoder_1_out4, decoder_1_out5,
       decoder_1_out6, decoder_1_out7, decoder_1_out8, decoder_1_out9, decoder_1_out10, decoder_1_out11,
       decoder_1_out12, decoder_1_out13, decoder_1_out14, decoder_1_out15;

  D_Flip_Flop #(.trigger("falling")) d_ff_1 (
    .clk(clock), .D(data), .Q(p0), .en(decoder_1_out0));  // open: Qn, preset, reset
  D_Flip_Flop #(.trigger("falling")) d_ff_2 (
    .clk(clock), .D(data), .Q(p1), .en(decoder_1_out1));  // open: Qn, preset, reset
  D_Flip_Flop #(.trigger("falling")) d_ff_3 (
    .clk(clock), .D(data), .Q(p2), .en(decoder_1_out2));  // open: Qn, preset, reset
  D_Flip_Flop #(.trigger("falling")) d_ff_4 (
    .clk(clock), .D(data), .Q(p3), .en(decoder_1_out3));  // open: Qn, preset, reset
  D_Flip_Flop #(.trigger("falling")) d_ff_5 (
    .clk(clock), .D(data), .Q(p4), .en(decoder_1_out4));  // open: Qn, preset, reset
  D_Flip_Flop #(.trigger("falling")) d_ff_6 (
    .clk(clock), .D(data), .Q(p5), .en(decoder_1_out5));  // open: Qn, preset, reset
  D_Flip_Flop #(.trigger("falling")) d_ff_7 (
    .clk(clock), .D(data), .Q(p6), .en(decoder_1_out6));  // open: Qn, preset, reset
  D_Flip_Flop #(.trigger("falling")) d_ff_8 (
    .clk(clock), .D(data), .Q(p7), .en(decoder_1_out7));  // open: Qn, preset, reset
  D_Flip_Flop #(.trigger("falling")) d_ff_9 (
    .clk(clock), .D(data), .Q(p8), .en(decoder_1_out8));  // open: Qn, preset, reset
  D_Flip_Flop #(.trigger("falling")) d_ff_10 (
    .clk(clock), .D(data), .Q(p9), .en(decoder_1_out9));  // open: Qn, preset, reset
  D_Flip_Flop #(.trigger("falling")) d_ff_11 (
    .clk(clock), .D(data), .Q(p10), .en(decoder_1_out10));  // open: Qn, preset, reset
  D_Flip_Flop #(.trigger("falling")) d_ff_12 (
    .clk(clock), .D(data), .Q(p11), .en(decoder_1_out11));  // open: Qn, preset, reset
  D_Flip_Flop #(.trigger("falling")) d_ff_13 (
    .clk(clock), .D(data), .Q(p12), .en(decoder_1_out12));  // open: Qn, preset, reset
  D_Flip_Flop #(.trigger("falling")) d_ff_14 (
    .clk(clock), .D(data), .Q(p13), .en(decoder_1_out13));  // open: Qn, preset, reset
  D_Flip_Flop #(.trigger("falling")) d_ff_15 (
    .clk(clock), .D(data), .Q(p14), .en(decoder_1_out14));  // open: Qn, preset, reset
  D_Flip_Flop #(.trigger("falling")) d_ff_16 (
    .clk(clock), .D(data), .Q(p15), .en(decoder_1_out15));  // open: Qn, preset, reset
  Decoder #(.select(4), .tristate("false")) decoder_1 (
    .out0(decoder_1_out0), .out1(decoder_1_out1), .out2(decoder_1_out2), .out3(decoder_1_out3),
    .out4(decoder_1_out4), .out5(decoder_1_out5), .out6(decoder_1_out6), .out7(decoder_1_out7),
    .out8(decoder_1_out8), .out9(decoder_1_out9), .out10(decoder_1_out10), .out11(decoder_1_out11),
    .out12(decoder_1_out12), .out13(decoder_1_out13), .out14(decoder_1_out14), .out15(decoder_1_out15),
    .sel(sel));
endmodule

module Register_File (
  input  [4:0] read_adr_4,
  input  [4:0] read_adr_3,
  input  [4:0] read_adr_2,
  input  [4:0] read_adr_1,
  input  write_enable,
  input  [4:0] write_adress,
  input  [31:0] write_data,
  output [31:0] read_out_4,
  output [31:0] read_out_1,
  output [31:0] read_out_2,
  output [31:0] read_out_3
);

  wire and_1_out, and_2_out, and_3_out, and_4_out, and_5_out, and_6_out, and_7_out, and_8_out, and_9_out,
       and_10_out, and_11_out, and_12_out, and_13_out, and_14_out, and_15_out, and_16_out, and_17_out,
       and_18_out, and_19_out, and_20_out, and_21_out, and_22_out, and_23_out, and_24_out, and_25_out,
       and_26_out, and_27_out, and_28_out, and_29_out, and_30_out, and_31_out, and_32_out, and_33_out,
       clock_1_out, decoder_1_out0, decoder_1_out1, decoder_1_out2, decoder_1_out3, decoder_1_out4,
       decoder_1_out5, decoder_1_out6, decoder_1_out7, decoder_1_out8, decoder_1_out9, decoder_1_out10,
       decoder_1_out11, decoder_1_out12, decoder_1_out13, decoder_1_out14, decoder_1_out15, decoder_2_out0,
       decoder_2_out1, decoder_2_out2, decoder_2_out3, decoder_2_out4, decoder_2_out5, decoder_2_out6,
       decoder_2_out7, decoder_2_out8, decoder_2_out9, decoder_2_out10, decoder_2_out11, decoder_2_out12,
       decoder_2_out13, decoder_2_out14, decoder_2_out15, not_1_out;
  wire [31:0] register_1_q, register_2_q, register_3_q, register_4_q, register_5_q, register_6_q,
       register_7_q, register_8_q, register_9_q, register_10_q, register_11_q, register_12_q, register_13_q,
       register_14_q, register_15_q, register_16_q, register_17_q, register_18_q, register_19_q,
       register_20_q, register_21_q, register_22_q, register_23_q, register_24_q, register_25_q,
       register_26_q, register_27_q, register_28_q, register_29_q, register_30_q, register_31_q;

  not not_1 (not_1_out, write_adress[4]);
  Decoder #(.select(4), .tristate("false")) decoder_1 (
    .out0(decoder_1_out0), .out1(decoder_1_out1), .out2(decoder_1_out2), .out3(decoder_1_out3),
    .out4(decoder_1_out4), .out5(decoder_1_out5), .out6(decoder_1_out6), .out7(decoder_1_out7),
    .out8(decoder_1_out8), .out9(decoder_1_out9), .out10(decoder_1_out10), .out11(decoder_1_out11),
    .out12(decoder_1_out12), .out13(decoder_1_out13), .out14(decoder_1_out14), .out15(decoder_1_out15),
    .sel(write_adress[3:0]));
  Decoder #(.select(4), .tristate("false")) decoder_2 (
    .out0(decoder_2_out0), .out1(decoder_2_out1), .out2(decoder_2_out2), .out3(decoder_2_out3),
    .out4(decoder_2_out4), .out5(decoder_2_out5), .out6(decoder_2_out6), .out7(decoder_2_out7),
    .out8(decoder_2_out8), .out9(decoder_2_out9), .out10(decoder_2_out10), .out11(decoder_2_out11),
    .out12(decoder_2_out12), .out13(decoder_2_out13), .out14(decoder_2_out14), .out15(decoder_2_out15),
    .sel(write_adress[3:0]));
  and and_1 (and_1_out, write_enable, write_adress[4]);
  and and_2 (and_2_out, write_enable, not_1_out);
  Clock #(.highDuration(1), .lowDuration(1)) clock_1 (.out(clock_1_out));
  and and_3 (and_3_out, decoder_1_out1, and_2_out);
  and and_4 (and_4_out, decoder_1_out2, and_2_out);
  and and_5 (and_5_out, decoder_1_out3, and_2_out);
  and and_6 (and_6_out, decoder_1_out4, and_2_out);
  and and_7 (and_7_out, decoder_1_out5, and_2_out);
  and and_8 (and_8_out, decoder_1_out6, and_2_out);
  and and_9 (and_9_out, decoder_1_out7, and_2_out);
  and and_10 (and_10_out, decoder_1_out8, and_2_out);
  and and_11 (and_11_out, decoder_1_out9, and_2_out);
  and and_12 (and_12_out, decoder_1_out10, and_2_out);
  and and_13 (and_13_out, decoder_1_out11, and_2_out);
  and and_14 (and_14_out, decoder_1_out12, and_2_out);
  and and_15 (and_15_out, decoder_1_out13, and_2_out);
  and and_16 (and_16_out, decoder_1_out14, and_2_out);
  and and_17 (and_17_out, decoder_1_out15, and_2_out);
  and and_18 (and_18_out, decoder_2_out0, and_1_out);
  and and_19 (and_19_out, decoder_2_out1, and_1_out);
  and and_20 (and_20_out, decoder_2_out2, and_1_out);
  and and_21 (and_21_out, decoder_2_out3, and_1_out);
  and and_22 (and_22_out, decoder_2_out4, and_1_out);
  and and_23 (and_23_out, decoder_2_out5, and_1_out);
  and and_24 (and_24_out, decoder_2_out6, and_1_out);
  and and_25 (and_25_out, decoder_2_out7, and_1_out);
  and and_26 (and_26_out, decoder_2_out8, and_1_out);
  and and_27 (and_27_out, decoder_2_out9, and_1_out);
  and and_28 (and_28_out, decoder_2_out10, and_1_out);
  and and_29 (and_29_out, decoder_2_out11, and_1_out);
  and and_30 (and_30_out, decoder_2_out12, and_1_out);
  and and_31 (and_31_out, decoder_2_out13, and_1_out);
  and and_32 (and_32_out, decoder_2_out14, and_1_out);
  and and_33 (and_33_out, decoder_2_out15, and_1_out);
  Register #(.width(32), .trigger("falling")) register_1 (
    .D(write_data), .en(and_4_out), .Q(register_1_q), .clk(clock_1_out));  // open: clr
  Register #(.width(32), .trigger("falling")) register_2 (
    .D(write_data), .en(and_6_out), .Q(register_2_q), .clk(clock_1_out));  // open: clr
  Register #(.width(32), .trigger("falling")) register_3 (
    .D(write_data), .en(and_8_out), .Q(register_3_q), .clk(clock_1_out));  // open: clr
  Register #(.width(32), .trigger("falling")) register_4 (
    .D(write_data), .en(and_10_out), .Q(register_4_q), .clk(clock_1_out));  // open: clr
  Register #(.width(32), .trigger("falling")) register_5 (
    .D(write_data), .en(and_12_out), .Q(register_5_q), .clk(clock_1_out));  // open: clr
  Register #(.width(32), .trigger("falling")) register_6 (
    .D(write_data), .en(and_14_out), .Q(register_6_q), .clk(clock_1_out));  // open: clr
  Register #(.width(32), .trigger("rising")) register_7 (
    .D(write_data), .en(and_16_out), .Q(register_7_q), .clk(clock_1_out));  // open: clr
  Register #(.width(32), .trigger("falling")) register_8 (
    .D(write_data), .en(and_18_out), .Q(register_8_q), .clk(clock_1_out));  // open: clr
  Register #(.width(32), .trigger("falling")) register_9 (
    .D(write_data), .en(and_20_out), .Q(register_9_q), .clk(clock_1_out));  // open: clr
  Register #(.width(32), .trigger("falling")) register_10 (
    .D(write_data), .en(and_22_out), .Q(register_10_q), .clk(clock_1_out));  // open: clr
  Register #(.width(32), .trigger("falling")) register_11 (
    .D(write_data), .en(and_24_out), .Q(register_11_q), .clk(clock_1_out));  // open: clr
  Register #(.width(32), .trigger("falling")) register_12 (
    .D(write_data), .en(and_26_out), .Q(register_12_q), .clk(clock_1_out));  // open: clr
  Register #(.width(32), .trigger("falling")) register_13 (
    .D(write_data), .en(and_28_out), .Q(register_13_q), .clk(clock_1_out));  // open: clr
  Register #(.width(32), .trigger("falling")) register_14 (
    .D(write_data), .en(and_30_out), .Q(register_14_q), .clk(clock_1_out));  // open: clr
  Register #(.width(32), .trigger("falling")) register_15 (
    .D(write_data), .en(and_32_out), .Q(register_15_q), .clk(clock_1_out));  // open: clr
  Register #(.width(32), .trigger("falling")) register_16 (
    .D(write_data), .en(and_3_out), .Q(register_16_q), .clk(clock_1_out));  // open: clr
  Register #(.width(32), .trigger("falling")) register_17 (
    .D(write_data), .en(and_5_out), .Q(register_17_q), .clk(clock_1_out));  // open: clr
  Register #(.width(32), .trigger("falling")) register_18 (
    .D(write_data), .en(and_7_out), .Q(register_18_q), .clk(clock_1_out));  // open: clr
  Register #(.width(32), .trigger("falling")) register_19 (
    .D(write_data), .en(and_9_out), .Q(register_19_q), .clk(clock_1_out));  // open: clr
  Register #(.width(32), .trigger("falling")) register_20 (
    .D(write_data), .en(and_11_out), .Q(register_20_q), .clk(clock_1_out));  // open: clr
  Register #(.width(32), .trigger("falling")) register_21 (
    .D(write_data), .en(and_13_out), .Q(register_21_q), .clk(clock_1_out));  // open: clr
  Register #(.width(32), .trigger("falling")) register_22 (
    .D(write_data), .en(and_15_out), .Q(register_22_q), .clk(clock_1_out));  // open: clr
  Register #(.width(32), .trigger("rising")) register_23 (
    .D(write_data), .en(and_17_out), .Q(register_23_q), .clk(clock_1_out));  // open: clr
  Register #(.width(32), .trigger("falling")) register_24 (
    .D(write_data), .en(and_19_out), .Q(register_24_q), .clk(clock_1_out));  // open: clr
  Register #(.width(32), .trigger("falling")) register_25 (
    .D(write_data), .en(and_21_out), .Q(register_25_q), .clk(clock_1_out));  // open: clr
  Register #(.width(32), .trigger("falling")) register_26 (
    .D(write_data), .en(and_23_out), .Q(register_26_q), .clk(clock_1_out));  // open: clr
  Register #(.width(32), .trigger("falling")) register_27 (
    .D(write_data), .en(and_25_out), .Q(register_27_q), .clk(clock_1_out));  // open: clr
  Register #(.width(32), .trigger("falling")) register_28 (
    .D(write_data), .en(and_27_out), .Q(register_28_q), .clk(clock_1_out));  // open: clr
  Register #(.width(32), .trigger("falling")) register_29 (
    .D(write_data), .en(and_29_out), .Q(register_29_q), .clk(clock_1_out));  // open: clr
  Register #(.width(32), .trigger("falling")) register_30 (
    .D(write_data), .en(and_31_out), .Q(register_30_q), .clk(clock_1_out));  // open: clr
  Register #(.width(32), .trigger("falling")) register_31 (
    .D(write_data), .en(and_33_out), .Q(register_31_q));  // open: clk, clr
  _32MUX u_32mux_1 (
    .D0({32{1'b0}}), .D1(register_16_q), .D2(register_1_q), .D3(register_17_q), .D4(register_2_q),
    .D5(register_18_q), .D6(register_3_q), .D7(register_19_q), .D8(register_4_q), .D9(register_20_q),
    .D10(register_5_q), .D11(register_21_q), .D12(register_6_q), .D13(register_22_q), .D14(register_7_q),
    .D15(register_23_q), .D16(register_8_q), .D17(register_24_q), .D18(register_9_q), .D19(register_25_q),
    .D20(register_10_q), .D21(register_26_q), .D22(register_11_q), .D23(register_27_q), .D24(register_12_q),
    .D25(register_28_q), .D26(register_13_q), .D27(register_29_q), .D28(register_14_q), .D29(register_30_q),
    .D30(register_15_q), .D31(register_31_q), .select(read_adr_4), .\output (read_out_4));
  _32MUX u_32mux_2 (
    .D0({32{1'b0}}), .D1(register_16_q), .D2(register_1_q), .D3(register_17_q), .D4(register_2_q),
    .D5(register_18_q), .D6(register_3_q), .D7(register_19_q), .D8(register_4_q), .D9(register_20_q),
    .D10(register_5_q), .D11(register_21_q), .D12(register_6_q), .D13(register_22_q), .D14(register_7_q),
    .D15(register_23_q), .D16(register_8_q), .D17(register_24_q), .D18(register_9_q), .D19(register_25_q),
    .D20(register_10_q), .D21(register_26_q), .D22(register_11_q), .D23(register_27_q), .D24(register_12_q),
    .D25(register_28_q), .D26(register_13_q), .D27(register_29_q), .D28(register_14_q), .D29(register_30_q),
    .D30(register_15_q), .D31(register_31_q), .select(read_adr_1), .\output (read_out_1));
  _32MUX u_32mux_3 (
    .D0({32{1'b0}}), .D1(register_16_q), .D2(register_1_q), .D3(register_17_q), .D4(register_2_q),
    .D5(register_18_q), .D6(register_3_q), .D7(register_19_q), .D8(register_4_q), .D9(register_20_q),
    .D10(register_5_q), .D11(register_21_q), .D12(register_6_q), .D13(register_22_q), .D14(register_7_q),
    .D15(register_23_q), .D16(register_8_q), .D17(register_24_q), .D18(register_9_q), .D19(register_25_q),
    .D20(register_10_q), .D21(register_26_q), .D22(register_11_q), .D23(register_27_q), .D24(register_12_q),
    .D25(register_28_q), .D26(register_13_q), .D27(register_29_q), .D28(register_14_q), .D29(register_30_q),
    .D30(register_15_q), .D31(register_31_q), .select(read_adr_2), .\output (read_out_2));
  _32MUX u_32mux_4 (
    .D0({32{1'b0}}), .D1(register_16_q), .D2(register_1_q), .D3(register_17_q), .D4(register_2_q),
    .D5(register_18_q), .D6(register_3_q), .D7(register_19_q), .D8(register_4_q), .D9(register_20_q),
    .D10(register_5_q), .D11(register_21_q), .D12(register_6_q), .D13(register_22_q), .D14(register_7_q),
    .D15(register_23_q), .D16(register_8_q), .D17(register_24_q), .D18(register_9_q), .D19(register_25_q),
    .D20(register_10_q), .D21(register_26_q), .D22(register_11_q), .D23(register_27_q), .D24(register_12_q),
    .D25(register_28_q), .D26(register_13_q), .D27(register_29_q), .D28(register_14_q), .D29(register_30_q),
    .D30(register_15_q), .D31(register_31_q), .select(read_adr_3), .\output (read_out_3));

  // Notes on the sheet:
  //   Write control
  //   Register Bank
  //   0
  //   2
  //   4
  //   6
  //   8
  //   10
  //   12
  //   14
  //   16
  //   18
  //   20
  //   22
  //   24
  //   26
  //   28
  //   30
  //   1
  //   3
  //   5
  //   7
  //   9
  //   11
  //   13
  //   15
  //   17
  //   19
  //   21
  //   23
  //   25
  //   27
  //   29
  //   31
endmodule

module Condition_Block (
  input  [4:0] flags,
  input  [2:0] cntl_from_ID,
  output output_to_IF
);

  Multiplexer #(.select(3), .width(1)) multiplexer_1 (
    .in0(1'b0), .in1(flags[0]), .in2(flags[1]), .in3(flags[2]), .in4(flags[3]), .in5(flags[4]), .in6(1'b1),
    .out(output_to_IF), .sel(cntl_from_ID));  // open: in7

  // Notes on the sheet:
  //   Ben Oztalay
  //   August, 2009
  //   reversed bit order of splitter out of convenience
endmodule

module ALUblock0 (
  input  Ai_1,
  input  A,
  input  Ai_1_2,
  input  B,
  input  [3:0] Cntl,
  output Cout,
  output S
);

  wire adder_1_s, and_1_out, multiplexer_1_out, not_1_out, or_1_out, xor_1_out;

  not not_1 (not_1_out, B);
  Multiplexer #(.select(1), .width(1)) multiplexer_1 (.in0(B), .in1(not_1_out), .out(multiplexer_1_out), .sel(Cntl[0]));
  Adder adder_1 (.Cout(Cout), .A(A), .B(multiplexer_1_out), .S(adder_1_s), .Cin(Cntl[0]));
  and and_1 (and_1_out, A, B);
  or or_1 (or_1_out, A, B);
  xor xor_1 (xor_1_out, A, B);
  Multiplexer #(.select(4), .width(1)) multiplexer_2 (
    .in0(adder_1_s), .in1(adder_1_s), .in2(and_1_out), .in3(or_1_out), .in4(xor_1_out), .in5(1'b0),
    .in6(1'b0), .in7(Ai_1), .in8(Ai_1_2), .in9(Ai_1), .out(S), .sel(Cntl));  // open: in10, in11, in12, in13, in14, in15

  // Notes on the sheet:
  //   +
endmodule

module ALUblock (
  input  Ai_1,
  input  A,
  input  Ai_1_2,
  input  B,
  input  Cin,
  input  [3:0] Cntl,
  output Cout,
  output S
);

  wire adder_1_s, and_1_out, multiplexer_1_out, not_1_out, or_1_out, xor_1_out;

  not not_1 (not_1_out, B);
  Multiplexer #(.select(1), .width(1)) multiplexer_1 (.in0(B), .in1(not_1_out), .out(multiplexer_1_out), .sel(Cntl[0]));
  Adder adder_1 (.Cout(Cout), .A(A), .B(multiplexer_1_out), .S(adder_1_s), .Cin(Cin));
  and and_1 (and_1_out, A, B);
  or or_1 (or_1_out, A, B);
  xor xor_1 (xor_1_out, A, B);
  Multiplexer #(.select(4), .width(1)) multiplexer_2 (
    .in0(adder_1_s), .in1(adder_1_s), .in2(and_1_out), .in3(or_1_out), .in4(xor_1_out), .in5(1'b0),
    .in6(Ai_1_2), .in7(Ai_1), .in8(Ai_1_2), .in9(Ai_1), .out(S), .sel(Cntl));  // open: in10, in11, in12, in13, in14, in15

  // Notes on the sheet:
  //   +
endmodule

module ALUblock31 (
  input  Ai_1,
  input  A,
  input  Ai_1_2,
  input  B,
  input  Cin,
  input  [3:0] Cntl,
  output Cout,
  output S
);

  wire adder_1_s, and_1_out, multiplexer_1_out, not_1_out, or_1_out, xor_1_out;

  not not_1 (not_1_out, B);
  Multiplexer #(.select(1), .width(1)) multiplexer_1 (.in0(B), .in1(not_1_out), .out(multiplexer_1_out), .sel(Cntl[0]));
  Adder adder_1 (.Cout(Cout), .A(A), .B(multiplexer_1_out), .S(adder_1_s), .Cin(Cin));
  and and_1 (and_1_out, A, B);
  xor xor_1 (xor_1_out, A, B);
  or or_1 (or_1_out, A, B);
  Multiplexer #(.select(4), .width(1)) multiplexer_2 (
    .in0(adder_1_s), .in1(adder_1_s), .in2(and_1_out), .in3(or_1_out), .in4(xor_1_out), .in5(1'b0),
    .in6(Ai_1_2), .in7(1'b0), .in8(Ai_1_2), .in9(Ai_1), .out(S), .sel(Cntl));  // open: in10, in11, in12, in13, in14, in15

  // Notes on the sheet:
  //   +
endmodule

module Adder (
  input  A,
  input  B,
  input  Cin,
  output Cout,
  output S
);

  wire and_1_out, and_2_out, xor_1_out;

  and and_1 (and_1_out, A, B);
  xor xor_1 (xor_1_out, A, B);
  and and_2 (and_2_out, xor_1_out, Cin);
  xor xor_2 (S, Cin, xor_1_out);
  or or_1 (Cout, and_1_out, and_2_out);
endmodule

module _32MUX (
  input  [4:0] select,
  input  [31:0] D0,
  input  [31:0] D1,
  input  [31:0] D2,
  input  [31:0] D3,
  input  [31:0] D4,
  input  [31:0] D5,
  input  [31:0] D6,
  input  [31:0] D7,
  input  [31:0] D8,
  input  [31:0] D9,
  input  [31:0] D10,
  input  [31:0] D11,
  input  [31:0] D12,
  input  [31:0] D13,
  input  [31:0] D14,
  input  [31:0] D15,
  input  [31:0] D16,
  input  [31:0] D17,
  input  [31:0] D18,
  input  [31:0] D19,
  input  [31:0] D20,
  input  [31:0] D21,
  input  [31:0] D22,
  input  [31:0] D23,
  input  [31:0] D24,
  input  [31:0] D25,
  input  [31:0] D26,
  input  [31:0] D27,
  input  [31:0] D28,
  input  [31:0] D29,
  input  [31:0] D30,
  input  [31:0] D31,
  output [31:0] \output 
);

  wire not_1_out;
  wire [3:0] controlled_buffer_1_out, controlled_buffer_2_out;
  wire [31:0] multiplexer_1_out, multiplexer_2_out;

  Multiplexer #(.select(4), .width(32)) multiplexer_1 (
    .in0(D0), .in1(D1), .in2(D2), .in3(D3), .in4(D4), .in5(D5), .in6(D6), .in7(D7), .in8(D8), .in9(D9),
    .in10(D10), .in11(D11), .in12(D12), .in13(D13), .in14(D14), .in15(D15), .out(multiplexer_1_out),
    .sel(controlled_buffer_1_out));
  not not_1 (not_1_out, select[4]);
  assign controlled_buffer_1_out = not_1_out ? select[3:0] : 4'bz;  // Controlled_Buffer controlled_buffer_1
  Multiplexer #(.select(4), .width(32)) multiplexer_2 (
    .in0(D16), .in1(D17), .in2(D18), .in3(D19), .in4(D20), .in5(D21), .in6(D22), .in7(D23), .in8(D24),
    .in9(D25), .in10(D26), .in11(D27), .in12(D28), .in13(D29), .in14(D30), .in15(D31),
    .out(multiplexer_2_out), .sel(controlled_buffer_2_out));
  assign controlled_buffer_2_out = select[4] ? select[3:0] : 4'bz;  // Controlled_Buffer controlled_buffer_2
  assign \output  = multiplexer_1_out | multiplexer_2_out;  // OR_Gate or_1, 32 bits wide
endmodule

module _16to32signex (
  input  [15:0] \input ,
  output [31:0] \output 
);


  assign \output  = {{17{\input [15]}}, \input [14:0]};
endmodule

module _21to32signex (
  input  [20:0] \input ,
  output [31:0] \output 
);


  assign \output  = {{12{\input [20]}}, \input [19:0]};
endmodule

module _32to24 (
  input  [31:0] \input ,
  output [23:0] \output 
);


  assign \output  = \input [23:0];
endmodule

module _32to4 (
  input  [31:0] \input ,
  output [3:0] \output 
);


  assign \output  = \input [3:0];
endmodule

module _32to7 (
  input  [31:0] \input ,
  output [6:0] \output 
);


  assign \output  = \input [6:0];
endmodule

module _5bitComp (
  input  [4:0] A,
  input  [4:0] B,
  output out_3
);

  wire or_1_out, xor_1_out, xor_2_out, xor_3_out, xor_4_out, xor_5_out;

  or or_1 (or_1_out, xor_1_out, xor_2_out, xor_3_out, xor_4_out, xor_5_out);
  not not_1 (out_3, or_1_out);
  xor xor_1 (xor_1_out, A[0], B[0]);
  xor xor_2 (xor_2_out, A[1], B[1]);
  xor xor_3 (xor_3_out, A[2], B[2]);
  xor xor_4 (xor_4_out, A[3], B[3]);
  xor xor_5 (xor_5_out, A[4], B[4]);
endmodule
